# Fritzing sketch ZenPongController (saved by Fritzing 1.0.8)
# Joystick: GND +5V VRx VRy SW license: CC-BY-SA-3.0
breadboards: 1

parts:
  UNO_R3_-_USB_power_/_PC = Arduino Uno (Rev3) - ICSP
  Joystick_GND_+5V_VRx_VRy_SW = Joystick: GND +5V VRx VRy SW
  VOLUME_10k_potentiometer = VOLUME: 10k potentiometer
  PASSIVE_buzzer_+_/_- = PASSIVE buzzer: + / -
  330_ohm_(five_bands) = Resistor [resistance=330 bands=5 tolerance=±1% package=THT]
  SLOWER_D4_/_GND = Pushbutton [package="[THT]"]
  FASTER_D5_/_GND = Pushbutton [package="[THT]"]
  VISUAL_D6_/_GND = Pushbutton [package="[THT]"]

nets:
  N1: UNO_R3_-_USB_power_/_PC.A0, Joystick_GND_+5V_VRx_VRy_SW.VRx
  N2: UNO_R3_-_USB_power_/_PC.A1, Joystick_GND_+5V_VRx_VRy_SW.VRy
  N3: UNO_R3_-_USB_power_/_PC.D8, 330_ohm_(five_bands).Pin_0
  GND: UNO_R3_-_USB_power_/_PC.GND, Joystick_GND_+5V_VRx_VRy_SW.GND, VOLUME_10k_potentiometer.B, PASSIVE_buzzer_+_/_-.-, SLOWER_D4_/_GND.Pin_4, FASTER_D5_/_GND.Pin_4, VISUAL_D6_/_GND.Pin_4
  N4: UNO_R3_-_USB_power_/_PC.D2, Joystick_GND_+5V_VRx_VRy_SW.SW
  N5: UNO_R3_-_USB_power_/_PC.D4, SLOWER_D4_/_GND.Pin_2
  N6: UNO_R3_-_USB_power_/_PC.D5_PWM, FASTER_D5_/_GND.Pin_2
  N7: UNO_R3_-_USB_power_/_PC.D6_PWM, VISUAL_D6_/_GND.Pin_2
  5V: UNO_R3_-_USB_power_/_PC.5V, Joystick_GND_+5V_VRx_VRy_SW.5V
  N8: VOLUME_10k_potentiometer.A, 330_ohm_(five_bands).Pin_1
  N9: VOLUME_10k_potentiometer.W, PASSIVE_buzzer_+_/_-.+

custom parts:
  Joystick: GND +5V VRx VRy SW: Joystick: GND +5V VRx VRy SW; derived diagram assets: CC BY-SA 3.0. This image was created with Fritzing.
  VOLUME: 10k potentiometer: VOLUME: 10k potentiometer; derived diagram assets: CC BY-SA 3.0. This image was created with Fritzing.
  PASSIVE buzzer: + / -: PASSIVE buzzer: + / -; derived diagram assets: CC BY-SA 3.0. This image was created with Fritzing.
